# Fritzing sketch wifi-therm-supply (saved by Fritzing 0.9.4)

parts:
  M1 = TP4056 Module [part_number=HW-107]
  M2 = MT3608 Module
  U1 = LIPO-1000mAh [package=lipo-1000]
  C1 = Capacitor Polarized [part_number="1000 uF" package=cpol-radial-1000uf-63v]
  D1 = SOLAR-IXYS [package=solarbit-12x1]
  U2 = V_REG_LD1117VXX [package=78xxl]

nets:
  N1: M1.pin1, D1.A
  N2: M1.pin2, M2.pin4
  N3: M1.pin3, U1.-
  N4: M1.pin4, U1.+
  N5: M1.pin5, M2.pin3
  N6: M1.pin6, D1.C
  N7: M2.pin1, C1.-, U2.GND
  N8: M2.pin2, C1.+, U2.IN

notes:
  3.3V
  2.6 - 4.5 V
  5.5 V
  0 - 6 V

custom parts:
  TP4056 Module: TP4056 Lithium Battery Charge Management Module Links: TP4056 website
  MT3608 Module: MT3608 Boost Converter Module Links: Aerosemi MT3608 2A Step Up Converter datasheet
